// Logisim project problem1.circ as structural Verilog: 1 circuit, main circuit main
module main (
  input  R,
  input  S,
  output Q,
  output Qbar
);

  nor nor_1 (Q, R, Qbar);
  nor nor_2 (Qbar, Q, S);
endmodule
