// Logisim project problem2.circ as structural Verilog: 1 circuit, main circuit main
module main (
  input  D,
  input  en,
  output Q,
  output Qbar
);

  wire nand_1_out, nand_2_out, not_1_out;

  not not_1 (not_1_out, D);
  nand nand_1 (nand_1_out, D, en);
  nand nand_2 (nand_2_out, not_1_out, en);
  nand nand_3 (Q, nand_1_out, Qbar);
  nand nand_4 (Qbar, Q, nand_2_out);
endmodule
