// Logisim project problem2_ver.circ as structural Verilog
module main (
  input  in_1,
  input  in_2,
  output out_3,
  output out_4
);

  problem2 problem2_1 (.D(in_1), .en(in_2), .Q(out_3), .Q_bar(out_4));
endmodule

// VHDL entity problem2, as the project stores it:
library IEEE;
use IEEE.STD_LOGIC_1164.ALL;

entity problem2 is
    Port (
        D     : in  STD_LOGIC;
        en    : in  STD_LOGIC;
        Q     : out STD_LOGIC;
        Q_bar : out STD_LOGIC
    );
end problem2;

architecture Behavioral of problem2 is
    signal q_reg : STD_LOGIC := '0';
begin

    process(D, en)
    begin
        if en = '1' then
            q_reg <= D;
        end if;
    end process;

    Q     <= q_reg;
    Q_bar <= not q_reg;

end Behavioral;
