// Logisim project problem3.circ as structural Verilog: 1 circuit, main circuit main
module main (
  input  D,
  input  clk,
  output out_3
);

  wire nand_1_out, nand_2_out, nand_3_out, nand_4_out, nand_5_out, nand_6_out, nand_8_out, not_1_out,
       not_2_out, not_3_out;

  not not_1 (not_1_out, D);
  not not_2 (not_2_out, clk);
  nand nand_1 (nand_1_out, not_1_out, not_2_out);
  nand nand_2 (nand_2_out, D, not_2_out);
  nand nand_3 (nand_3_out, nand_2_out, nand_4_out);
  nand nand_4 (nand_4_out, nand_3_out, nand_1_out);
  not not_3 (not_3_out, nand_3_out);
  nand nand_5 (nand_5_out, nand_3_out, clk);
  nand nand_6 (nand_6_out, not_3_out, clk);
  nand nand_7 (out_3, nand_5_out, nand_8_out);
  nand nand_8 (nand_8_out, out_3, nand_6_out);
endmodule
