// Logisim project problem4.circ as structural Verilog: 1 circuit, main circuit main
module main (
  input  J,
  input  CLK,
  input  K,
  input  in_4,
  output Q,
  output Qbar
);

  wire nand_1_out, nand_2_out, nand_3_out, nand_4_out, nand_5_out, nand_6_out, not_1_out, not_2_out;

  not not_1 (not_1_out, CLK);
  nand nand_1 (nand_1_out, J, not_1_out, Qbar);
  nand nand_2 (nand_2_out, Q, not_1_out, K);
  nand nand_3 (nand_3_out, nand_1_out, nand_4_out);
  nand nand_4 (nand_4_out, nand_3_out, in_4, nand_2_out);
  nand nand_5 (nand_5_out, nand_3_out, not_2_out);
  not not_2 (not_2_out, not_1_out);
  nand nand_6 (nand_6_out, nand_4_out, not_2_out);
  nand nand_7 (Q, nand_5_out, Qbar);
  nand nand_8 (Qbar, Q, in_4, nand_6_out);
endmodule
