// Logisim project problem5.circ as structural Verilog: 1 circuit, main circuit main
module main (
  input  set,
  input  D,
  input  clk,
  input  clr,
  output q,
  output qbar
);

  wire and_1_out, nand_1_out, nand_2_out, nand_3_out, nand_4_out, not_1_out, not_2_out;

  not not_1 (not_1_out, clr);
  and and_1 (and_1_out, set, not_1_out);
  nand nand_1 (nand_1_out, not_2_out, nand_3_out, nand_2_out);
  not not_2 (not_2_out, and_1_out);
  nand nand_2 (nand_2_out, D, not_1_out, nand_4_out);
  nand nand_3 (nand_3_out, nand_1_out, clk, not_1_out);
  nand nand_4 (nand_4_out, nand_3_out, clk, not_1_out);
  nand nand_5 (q, not_2_out, nand_3_out, qbar);
  nand nand_6 (qbar, q, nand_4_out, not_1_out);
endmodule
